# Fritzing sketch SMART WATERFLOW CONTROL AND MONITORING SYSTEM (saved by Fritzing 0.9.3b)
breadboards: 1

parts:
  U1 = A3144 Hall Effect Sensor. [package="UA [THT]"]
  LCD1 = LCD screen
  Part1 = Arduino Uno (Rev3)

nets:
  VDD: U1.+Vsupply, LCD1.VDD, LCD1.LED+, Part1.5V
  GND: U1.GND, LCD1.VSS, LCD1.V0, LCD1.R/W, LCD1.LED-, Part1.GND
  N1: U1.Out, Part1.A0
  N2: LCD1.RS, Part1.D7
  N3: LCD1.E, Part1.D6_PWM
  N4: LCD1.DB4, Part1.D5_PWM
  N5: LCD1.DB5, Part1.D4
  N6: LCD1.DB6, Part1.D3_PWM

notes:
  DESGNED BY HAB.SAM
  WATER FLOW SENSOR/
  HALL EFFECTS SENSOR
  16X2 LCD DISPLAY

custom parts:
  A3144 Hall Effect Sensor.: Allegro A3144 hall effect switch for high temperature operation.

// code stored in the sketch: SMART WATERFLOW CONTROL AND MONITORING SYSTEM 1.ino
#include <LiquidCrystal.h>
LiquidCrystal lcd(7, 6, 5, 4, 3, 2);
int X;
int Y;
float TIME = 0;
float FREQUENCY = 0;
float WATER = 0;
float TOTAL = 0;
float LS = 0;
const int input = A0;
void setup()
{
Serial.begin(9600);
lcd.begin(16, 2);
lcd.clear();
lcd.setCursor(0,0);
lcd.print("Water Flow Meter");
lcd.setCursor(0,1);
lcd.print("****************");
delay(2000);
pinMode(input,INPUT);
}
void loop()
{
X = pulseIn(input, HIGH);
Y = pulseIn(input, LOW);
TIME = X + Y;
FREQUENCY = 1000000/TIME;
WATER = FREQUENCY/7.5;
LS = WATER/60;
if(FREQUENCY >= 0)
{
if(isinf(FREQUENCY))
{
lcd.clear();
lcd.setCursor(0,0);
lcd.print("VOL. :0.00");
lcd.setCursor(0,1);
lcd.print("TOTAL:");
lcd.print( TOTAL);
lcd.print(" L");
}
else
{
TOTAL = TOTAL + LS;
Serial.println(FREQUENCY);
lcd.clear();
lcd.setCursor(0,0);
lcd.print("VOL.: ");
lcd.print(WATER);
lcd.print(" L/M");
lcd.setCursor(0,1);
lcd.print("TOTAL:");
lcd.print( TOTAL);
lcd.print( "L");
}
}
delay(1000);
}
